# Fritzing sketch awesomeplayer (saved by Fritzing 0.8.7b)
circuit board: 8.46667cm x 5.64444cm
breadboards: 1

parts:
  Part1 = Arduino Uno (Rev3)
  LED1 = LED - 5mm [color="Green (570nm)" package="5 mm [THT]"]
  LED2 = LED - 5mm [color="Green (570nm)" package="5 mm [THT]"]
  LED3 = LED - 5mm [color="Yellow (595nm)" package="5 mm [THT]"]
  LED4 = LED - 5mm [color="Yellow (595nm)" package="5 mm [THT]"]
  LED5 = LED - 5mm [color="Red (633nm)" package="5 mm [THT]"]
  LED6 = LED - 5mm [color="Red (633nm)" package="5 mm [THT]"]
  R1 = Resistor [tolerance=±5% resistance=220 package=THT]
  R2 = Resistor [tolerance=±5% resistance=220 package=THT]
  R3 = Resistor [tolerance=±5% resistance=220 package=THT]
  R4 = Resistor [tolerance=±5% resistance=220 package=THT]
  R5 = Resistor [tolerance=±5% resistance=220 package=THT]
  R6 = Resistor [tolerance=±5% resistance=220 package=THT]
  R7 = Resistor [tolerance=±5% resistance=220 package=THT]
  R8 = Resistor [tolerance=±5% resistance=220 package=THT]
  Q1 = NPN-Transistor [package="TO92 [THT]"]
  C1 = Tantalum Capacitor [capacitance=0.1µF package="100 mil [THT, tantalum]"]
  R9 = Resistor [tolerance=±5% resistance=10k package=THT]
  J2 = Piezo Speaker
  R10 = Resistor [tolerance=±5% resistance=100k package=THT]
  S1 = Pushbutton [package=THT]
  SPKR1 = Loudspeaker
  R11 = Resistor [tolerance=±5% resistance=100k package=THT]
  S2 = Pushbutton [package=THT]

nets:
  N1: Part1.D9_PWM, R9.Pin_0
  N2: Part1.D11_PWM/MOSI, R7.Pin_0
  N3: Part1.D12/MISO, R11.Pin_1, S2.leg1
  N4: Part1.D13/SCK, R10.Pin_1, S1.leg1
  N5: Part1.GND, LED1.cathode, LED2.cathode, LED3.cathode, LED4.cathode, LED5.cathode, LED6.cathode, Q1.B, C1.+, R9.Pin_1, J2.pin1, R10.Pin_0, R11.Pin_0
  N6: Part1.D2, R1.Pin_0
  N7: Part1.D3_PWM, R3.Pin_0
  N8: Part1.D4, R4.Pin_0
  N9: Part1.D5_PWM, R2.Pin_0
  N10: Part1.D6_PWM, R5.Pin_0
  N11: Part1.D7, R6.Pin_0
  N12: Part1.5V, R8.Pin_1, S1.leg0, SPKR1.pin1, SPKR1.pin2, S2.leg0
  N13: LED1.anode, R6.Pin_1
  N14: LED2.anode, R5.Pin_1
  N15: LED3.anode, R2.Pin_1
  N16: LED4.anode, R4.Pin_1
  N17: LED5.anode, R3.Pin_1
  N18: LED6.anode, R1.Pin_1
  N19: R7.Pin_1, J2.pin2
  N20: R8.Pin_0, Q1.E
  N21: Q1.C, C1.-
